// Logisim project bloco_1_atualizado.circ as structural Verilog: 1 circuit, main circuit main
module main (
  input  Q1,
  input  Q2,
  input  Q3,
  input  Q4,
  input  REQ,
  input  RW,
  output LD
);

  wire and_1_out, and_2_out, and_3_out, and_4_out, and_5_out, and_6_out, not_1_out, not_2_out, not_3_out,
       not_4_out, not_5_out, not_6_out, not_7_out, not_8_out, not_9_out, not_10_out, not_11_out;

  not not_1 (not_1_out, Q1);
  not not_2 (not_2_out, Q2);
  not not_3 (not_3_out, Q3);
  not not_4 (not_4_out, Q4);
  not not_5 (not_5_out, REQ);
  not not_6 (not_6_out, Q1);
  not not_7 (not_7_out, Q3);
  not not_8 (not_8_out, RW);
  not not_9 (not_9_out, Q3);
  not not_10 (not_10_out, Q3);
  not not_11 (not_11_out, RW);
  and and_1 (and_1_out, not_1_out, not_2_out, not_3_out, not_4_out, not_5_out);
  and and_2 (and_2_out, not_6_out, not_7_out, Q4, not_8_out);
  and and_3 (and_3_out, Q2, not_9_out, REQ, RW);
  and and_4 (and_4_out, Q2, not_10_out, Q4);
  and and_5 (and_5_out, Q1, Q3, Q4, REQ, not_11_out);
  and and_6 (and_6_out, Q1, Q2);
  or or_1 (LD, and_1_out, and_2_out, and_3_out, and_4_out, and_5_out, and_6_out);
endmodule
