// Logisim project bloco_2.circ as structural Verilog: 1 circuit, main circuit main
module main (
  input  Q1,
  input  Q2,
  input  Q3,
  input  Q4,
  output P1,
  output P2,
  output P3,
  output P4
);

  wire and_1_out, and_2_out, not_1_out, not_2_out, not_3_out, not_4_out, not_5_out;

  not not_1 (not_1_out, Q1);
  not not_2 (not_2_out, Q2);
  and and_1 (and_1_out, not_1_out, not_2_out, Q4);
  not not_3 (not_3_out, Q1);
  and and_2 (and_2_out, not_3_out, Q2, not_4_out);
  not not_4 (not_4_out, Q4);
  not not_5 (not_5_out, Q2);
  and and_3 (P3, not_5_out, Q4);
  or or_1 (P2, and_1_out, and_2_out);

  assign P1 = Q3;
  assign P4 = Q3;
endmodule
