// Logisim project bloco_cl (copy).circ as structural Verilog: 1 circuit, main circuit main
module main (
  input  Q7,
  input  Q6,
  input  Q5,
  input  Q4,
  input  Q3,
  input  Q2,
  input  Q1,
  input  E0,
  input  E1,
  input  REQ,
  input  RW,
  output CL
);

  wire and_1_out, and_2_out, and_3_out, and_4_out, and_5_out, not_1_out, not_2_out, not_3_out, not_4_out,
       not_5_out, not_6_out, not_7_out, not_8_out;

  not not_1 (not_1_out, Q5);
  not not_2 (not_2_out, Q1);
  not not_3 (not_3_out, Q5);
  not not_4 (not_4_out, E0);
  not not_5 (not_5_out, E1);
  not not_6 (not_6_out, Q5);
  not not_7 (not_7_out, RW);
  not not_8 (not_8_out, Q5);
  and and_1 (and_1_out, not_1_out, not_2_out);
  and and_2 (and_2_out, not_3_out, not_4_out, not_5_out, REQ);
  and and_3 (and_3_out, not_6_out, E1, REQ, not_7_out);
  and and_4 (and_4_out, not_8_out, E0, REQ, RW);
  and and_5 (and_5_out, Q5, Q1);
  or or_1 (CL, and_1_out, and_2_out, and_3_out, and_4_out, Q2, Q3, Q4, and_5_out, Q6, Q7);
endmodule
