// Logisim project bloco_cl_fix.circ as structural Verilog: 1 circuit, main circuit main
module main (
  input  Q4,
  input  Q3,
  input  Q2,
  input  Q1,
  input  E1,
  input  E0,
  input  REQ,
  input  RW,
  output CL
);

  wire and_1_out, and_2_out, and_3_out, and_4_out, and_5_out, and_6_out, and_7_out, and_8_out, and_9_out,
       and_10_out, and_11_out, not_1_out, not_2_out, not_3_out, not_4_out, not_5_out, not_6_out, not_7_out,
       not_8_out, not_9_out, not_10_out;

  not not_1 (not_1_out, Q2);
  and and_1 (and_1_out, not_1_out, not_2_out);
  not not_2 (not_2_out, Q1);
  not not_3 (not_3_out, Q4);
  and and_2 (and_2_out, not_3_out, not_4_out, REQ);
  not not_4 (not_4_out, Q2);
  not not_5 (not_5_out, Q3);
  and and_3 (and_3_out, not_5_out, not_6_out, E0);
  not not_6 (not_6_out, Q1);
  and and_4 (and_4_out, E0, REQ, RW);
  not not_7 (not_7_out, Q1);
  and and_5 (and_5_out, not_7_out, E1);
  and and_6 (and_6_out, E1, REQ, not_8_out);
  not not_8 (not_8_out, RW);
  and and_7 (and_7_out, E1, E0);
  and and_8 (and_8_out, Q2, Q1);
  and and_9 (and_9_out, Q3, not_9_out);
  not not_9 (not_9_out, Q2);
  and and_10 (and_10_out, Q4, not_10_out);
  not not_10 (not_10_out, Q1);
  and and_11 (and_11_out, Q4, E0);
  or or_1 (CL, and_1_out, and_2_out, and_3_out, and_4_out, and_5_out, and_6_out, and_7_out, and_8_out, and_9_out, and_10_out, and_11_out);
endmodule
