// Logisim project bloco_conversor_one_hot_to_bin.circ as structural Verilog: 1 circuit, main circuit main
module main (
  input  Q9,
  input  Q8,
  input  Q7,
  input  Q6,
  input  Q5,
  input  Q4,
  input  Q3,
  input  Q2,
  input  Q1,
  output Q4_2,
  output Q3_2,
  output Q2_2,
  output Q1_2
);

  wire not_1_out, not_2_out, not_3_out, not_4_out, not_5_out, not_6_out, not_7_out, not_8_out, not_9_out,
       not_10_out, not_11_out, not_12_out, not_13_out, not_14_out, not_15_out, not_16_out, not_17_out,
       not_18_out, not_19_out, not_20_out, not_21_out;

  not not_1 (not_1_out, Q7);
  not not_2 (not_2_out, Q6);
  not not_3 (not_3_out, Q5);
  not not_4 (not_4_out, Q4);
  not not_5 (not_5_out, Q3);
  not not_6 (not_6_out, Q2);
  not not_7 (not_7_out, Q1);
  not not_8 (not_8_out, Q9);
  not not_9 (not_9_out, Q8);
  not not_10 (not_10_out, Q3);
  not not_11 (not_11_out, Q2);
  not not_12 (not_12_out, Q1);
  not not_13 (not_13_out, Q9);
  not not_14 (not_14_out, Q8);
  not not_15 (not_15_out, Q5);
  not not_16 (not_16_out, Q4);
  not not_17 (not_17_out, Q1);
  not not_18 (not_18_out, Q8);
  not not_19 (not_19_out, Q6);
  not not_20 (not_20_out, Q4);
  not not_21 (not_21_out, Q2);
  and and_1 (Q4_2, not_1_out, not_2_out, not_3_out, not_4_out, not_5_out, not_6_out, not_7_out);
  and and_2 (Q3_2, not_8_out, not_9_out, not_10_out, not_11_out, not_12_out);
  and and_3 (Q2_2, not_13_out, not_14_out, not_15_out, not_16_out, not_17_out);
  and and_4 (Q1_2, not_18_out, not_19_out, not_20_out, not_21_out);
endmodule
