// Logisim project bloco_mef (copy).circ as structural Verilog: 1 circuit, main circuit main
module main (
  input  Q7,
  input  Q6,
  input  Q5,
  input  Q4,
  input  Q3,
  input  Q2,
  input  Q1,
  input  REQ,
  input  RW,
  output S0,
  output S1
);

  wire and_1_out, and_2_out, and_3_out, and_4_out, and_5_out, and_6_out, and_7_out, and_8_out, and_9_out,
       and_10_out, and_11_out, and_12_out, and_13_out, and_14_out, and_15_out, and_16_out, and_17_out,
       and_18_out, and_19_out, and_20_out, and_21_out, and_22_out, and_23_out, and_24_out, and_25_out,
       and_26_out, and_27_out, and_28_out, and_29_out, and_30_out, and_31_out, and_32_out, and_33_out,
       and_34_out, and_35_out, and_36_out, and_37_out, and_38_out, and_39_out, and_40_out, and_41_out,
       and_42_out, and_43_out, and_44_out, and_45_out, and_46_out, and_47_out, and_48_out, and_49_out,
       and_50_out, and_51_out, and_52_out, and_53_out, and_54_out, and_55_out, and_56_out, button_1_out, E0,
       E1, not_1_out, not_2_out, not_3_out, not_4_out, not_5_out, not_6_out, not_7_out, not_8_out, not_9_out,
       not_10_out, not_11_out, not_12_out, not_13_out, not_14_out, not_15_out, not_16_out, not_17_out,
       not_18_out, or_1_out, or_2_out;

  not not_1 (not_1_out, E1);
  not not_2 (not_2_out, RW);
  not not_3 (not_3_out, REQ);
  not not_4 (not_4_out, RW);
  not not_5 (not_5_out, E1);
  not not_6 (not_6_out, E1);
  not not_7 (not_7_out, E1);
  not not_8 (not_8_out, E0);
  not not_9 (not_9_out, RW);
  not not_10 (not_10_out, E0);
  not not_11 (not_11_out, REQ);
  not not_12 (not_12_out, E0);
  not not_13 (not_13_out, E0);
  not not_14 (not_14_out, E0);
  not not_15 (not_15_out, E1);
  not not_16 (not_16_out, E0);
  not not_17 (not_17_out, E0);
  not not_18 (not_18_out, E0);
  and and_1 (and_1_out, Q1, not_1_out, REQ, not_2_out);
  and and_2 (and_2_out, Q1, E0, E1);
  and and_3 (and_3_out, Q2, not_3_out);
  and and_4 (and_4_out, Q2, not_4_out);
  and and_5 (and_5_out, Q2, E1);
  and and_6 (and_6_out, Q2, E0);
  and and_7 (and_7_out, Q2, Q1);
  and and_8 (and_8_out, Q3, not_5_out);
  and and_9 (and_9_out, Q3, E0);
  and and_10 (and_10_out, Q3, Q1);
  and and_11 (and_11_out, Q4, not_6_out);
  and and_12 (and_12_out, Q4, E0);
  and and_13 (and_13_out, Q4, Q1);
  and and_14 (and_14_out, Q4, Q3);
  and and_15 (and_15_out, Q5, not_7_out);
  and and_16 (and_16_out, Q5, E0);
  and and_17 (and_17_out, Q5, Q1);
  and and_18 (and_18_out, Q5, Q3);
  and and_19 (and_19_out, Q5, Q4);
  and and_20 (and_20_out, Q7, not_8_out);
  and and_21 (and_21_out, Q7, REQ, not_9_out);
  and and_22 (and_22_out, Q7, E1);
  and and_23 (and_23_out, Q7, Q1);
  and and_24 (and_24_out, Q1, not_10_out, REQ, RW);
  and and_25 (and_25_out, Q1, E0, E1);
  and and_26 (and_26_out, Q2, not_11_out);
  and and_27 (and_27_out, Q2, RW);
  and and_28 (and_28_out, Q2, E1);
  and and_29 (and_29_out, Q2, E0);
  and and_30 (and_30_out, Q2, Q1);
  and and_31 (and_31_out, Q3, not_12_out);
  and and_32 (and_32_out, Q3, E1);
  and and_33 (and_33_out, Q3, Q1);
  and and_34 (and_34_out, Q4, not_13_out);
  and and_35 (and_35_out, Q4, E1);
  and and_36 (and_36_out, Q4, Q1);
  and and_37 (and_37_out, Q4, Q3);
  and and_38 (and_38_out, Q5, not_14_out, not_15_out);
  and and_39 (and_39_out, Q5, not_16_out, REQ, RW);
  and and_40 (and_40_out, Q5, E0, E1);
  and and_41 (and_41_out, Q5, Q1);
  and and_42 (and_42_out, Q5, Q3);
  and and_43 (and_43_out, Q5, Q4);
  and and_44 (and_44_out, Q6, not_17_out);
  and and_45 (and_45_out, Q6, E1);
  and and_46 (and_46_out, Q6, Q1);
  and and_47 (and_47_out, Q6, Q3);
  and and_48 (and_48_out, Q6, Q4);
  and and_49 (and_49_out, Q6, Q5);
  and and_50 (and_50_out, Q7, not_18_out);
  and and_51 (and_51_out, Q7, E1);
  and and_52 (and_52_out, Q7, Q1);
  and and_53 (and_53_out, Q7, Q3);
  and and_54 (and_54_out, Q7, Q4);
  and and_55 (and_55_out, Q7, Q5);
  and and_56 (and_56_out, Q7, Q6);
  or or_1 (or_1_out, and_24_out, and_25_out, and_26_out, and_27_out, and_28_out, and_29_out, and_30_out, and_31_out, and_32_out, and_33_out, and_34_out, and_35_out, and_36_out, and_37_out, and_38_out, and_39_out, and_40_out);
  or or_2 (or_2_out, and_41_out, and_42_out, and_43_out, and_44_out, and_45_out, and_46_out, and_47_out, and_48_out, and_49_out, and_50_out, and_51_out, and_52_out, and_53_out, and_54_out, and_55_out, and_56_out);
  Button button_1 (.out(button_1_out));
  or or_3 (S0, and_1_out, and_2_out, and_3_out, and_4_out, and_5_out, and_6_out, and_7_out, and_8_out, and_9_out, and_10_out, and_11_out, and_12_out, and_13_out, and_14_out, and_15_out, and_16_out, and_17_out, and_18_out, and_19_out, Q6, and_20_out, and_21_out, and_22_out, and_23_out);
  or or_4 (S1, or_1_out, or_2_out);
  // Probe on E1
  // Probe on E0
  D_Flip_Flop d_ff_1 (.clk(button_1_out), .D(S0), .Q(E0));  // open: Qn, preset, en, reset
  D_Flip_Flop d_ff_2 (.clk(button_1_out), .D(S1), .Q(E1));  // open: Qn, preset, en, reset
endmodule
