// Logisim project bloco_mef_fix (copy).circ as structural Verilog: 1 circuit, main circuit main
module main (
  input  Q4,
  input  Q3,
  input  Q2,
  input  Q1,
  input  E1,
  input  E0,
  input  REQ,
  input  RW,
  output S1,
  output S0
);

  wire and_1_out, and_2_out, and_3_out, and_4_out, and_5_out, and_6_out, and_7_out, and_8_out, and_9_out,
       and_10_out, and_11_out, and_12_out, and_13_out, and_14_out, and_15_out, and_16_out, and_17_out,
       and_18_out, and_19_out, and_20_out, and_21_out, and_22_out, and_23_out, and_24_out, and_25_out,
       and_26_out, not_1_out, not_2_out, not_3_out, not_4_out, not_5_out, not_6_out, not_7_out, not_8_out,
       not_9_out, not_10_out, not_11_out, not_12_out, not_13_out, not_14_out, not_15_out, not_16_out,
       not_17_out, not_18_out, not_19_out, not_20_out, not_21_out, not_22_out, not_23_out, not_24_out,
       not_25_out;

  not not_1 (not_1_out, Q4);
  not not_2 (not_2_out, E1);
  not not_3 (not_3_out, E0);
  not not_4 (not_4_out, RW);
  not not_5 (not_5_out, E0);
  not not_6 (not_6_out, Q2);
  not not_7 (not_7_out, E0);
  not not_8 (not_8_out, Q1);
  not not_9 (not_9_out, E1);
  not not_10 (not_10_out, Q1);
  not not_11 (not_11_out, RW);
  not not_12 (not_12_out, Q4);
  not not_13 (not_13_out, Q3);
  not not_14 (not_14_out, Q2);
  not not_15 (not_15_out, E0);
  not not_16 (not_16_out, E1);
  not not_17 (not_17_out, Q2);
  not not_18 (not_18_out, Q1);
  not not_19 (not_19_out, E1);
  not not_20 (not_20_out, Q2);
  not not_21 (not_21_out, E1);
  not not_22 (not_22_out, E0);
  not not_23 (not_23_out, Q1);
  not not_24 (not_24_out, Q1);
  not not_25 (not_25_out, E1);
  and and_1 (and_1_out, E1, E0, REQ, RW);
  and and_2 (and_2_out, not_1_out, Q1, not_2_out, not_3_out, REQ, not_4_out);
  and and_3 (and_3_out, Q1, E1, REQ, RW);
  and and_4 (and_4_out, Q1, E1, E0);
  and and_5 (and_5_out, Q2, E1);
  and and_6 (and_6_out, Q2, Q1, not_5_out);
  and and_7 (and_7_out, Q3, not_6_out, not_7_out);
  and and_8 (and_8_out, Q3, E1);
  and and_9 (and_9_out, Q3, Q2, Q1);
  and and_10 (and_10_out, Q4, not_8_out, not_9_out);
  and and_11 (and_11_out, Q4, not_10_out, REQ, not_11_out);
  and and_12 (and_12_out, Q4, E0);
  and and_13 (and_13_out, Q4, Q1, E1);
  and and_14 (and_14_out, E1, E0, REQ, RW);
  and and_15 (and_15_out, not_12_out, not_13_out, not_14_out, Q1, not_15_out, REQ, RW);
  and and_16 (and_16_out, Q1, E1, E0);
  and and_17 (and_17_out, Q2, E0);
  and and_18 (and_18_out, Q2, Q1, not_16_out);
  and and_19 (and_19_out, Q3, not_17_out, not_18_out, not_19_out);
  and and_20 (and_20_out, Q3, not_20_out, not_21_out, not_22_out);
  and and_21 (and_21_out, Q3, not_23_out, E0);
  and and_22 (and_22_out, Q3, E0, REQ, RW);
  and and_23 (and_23_out, Q4, not_24_out, not_25_out);
  and and_24 (and_24_out, Q4, E0);
  and and_25 (and_25_out, Q4, Q2);
  and and_26 (and_26_out, Q4, Q3);
  or or_1 (S1, and_1_out, and_2_out, and_3_out, and_4_out, and_5_out, and_6_out, and_7_out, and_8_out, and_9_out, and_10_out, and_11_out, and_12_out, and_13_out);
  or or_2 (S0, and_14_out, and_15_out, and_16_out, and_17_out, and_18_out, and_19_out, and_20_out, and_21_out, and_22_out, and_23_out, and_24_out, and_25_out, and_26_out);
endmodule
