// Logisim project bloco_mef_fix.circ as structural Verilog
module main (
  input  Q9S,
  input  Q8S,
  input  Q7S,
  input  Q6S,
  input  Q5S,
  input  Q4S,
  input  Q3S,
  input  Q2S,
  input  Q1S,
  input  REQ,
  input  RW,
  output DOUT,
  output DA,
  output WE,
  output CL,
  output S1,
  output WC,
  output Q4,
  output C0,
  output Q3,
  output C1,
  output Q2,
  output Q1,
  output S0
);

  wire and_1_out, and_2_out, and_3_out, and_4_out, and_5_out, and_6_out, and_7_out, and_8_out, and_9_out,
       and_10_out, and_11_out, and_12_out, and_13_out, and_14_out, and_15_out, and_16_out, and_17_out,
       and_18_out, and_19_out, and_20_out, and_21_out, and_22_out, and_23_out, and_24_out, and_25_out,
       and_26_out, and_27_out, and_28_out, and_29_out, and_30_out, and_31_out, and_32_out, and_33_out,
       and_34_out, and_35_out, and_36_out, and_37_out, and_42_out, and_43_out, and_44_out, and_45_out,
       and_46_out, and_47_out, and_48_out, and_49_out, and_50_out, and_51_out, and_52_out, and_53_out,
       button_1_out, E0, E1, not_1_out, not_2_out, not_3_out, not_4_out, not_5_out, not_6_out, not_7_out,
       not_8_out, not_9_out, not_10_out, not_11_out, not_12_out, not_13_out, not_14_out, not_15_out,
       not_16_out, not_17_out, not_18_out, not_19_out, not_20_out, not_21_out, not_22_out, not_23_out,
       not_24_out, not_25_out, not_26_out, not_27_out, not_28_out, not_29_out, not_30_out, not_31_out,
       not_32_out, not_33_out, not_34_out, not_35_out, not_36_out, not_37_out, not_38_out, not_39_out,
       not_40_out, not_41_out, not_42_out, not_43_out, not_44_out, not_45_out, not_46_out, not_47_out,
       not_48_out, not_49_out, not_50_out, not_51_out, not_52_out, not_53_out, not_54_out, not_55_out,
       not_56_out, not_57_out, not_58_out, not_59_out, not_60_out, not_61_out, not_62_out, not_63_out,
       not_64_out, not_65_out, not_66_out, not_67_out, not_68_out, not_69_out, not_70_out, not_71_out,
       not_72_out, not_73_out, not_74_out, not_75_out, not_76_out, not_77_out, not_78_out, not_79_out,
       not_80_out, not_81_out, not_82_out, not_83_out, not_84_out;

  not not_1 (not_1_out, Q4);
  not not_2 (not_2_out, E0);
  not not_3 (not_3_out, RW);
  not not_4 (not_4_out, Q3);
  not not_5 (not_5_out, Q2);
  not not_6 (not_6_out, Q3);
  not not_7 (not_7_out, E0);
  not not_8 (not_8_out, E0);
  not not_9 (not_9_out, Q2);
  not not_10 (not_10_out, E0);
  not not_11 (not_11_out, Q1);
  not not_12 (not_12_out, E1);
  not not_13 (not_13_out, Q1);
  not not_14 (not_14_out, RW);
  not not_15 (not_15_out, Q4);
  not not_16 (not_16_out, E1);
  not not_17 (not_17_out, Q3);
  not not_18 (not_18_out, Q3);
  not not_19 (not_19_out, Q2);
  not not_20 (not_20_out, Q3);
  not not_21 (not_21_out, E1);
  not not_22 (not_22_out, Q2);
  not not_23 (not_23_out, Q1);
  not not_24 (not_24_out, E1);
  not not_25 (not_25_out, E1);
  not not_26 (not_26_out, E0);
  not not_27 (not_27_out, Q1);
  not not_28 (not_28_out, E1);
  and and_1 (and_1_out, E1, E0, REQ, RW);
  and and_2 (and_2_out, not_1_out, Q1, not_2_out, REQ, not_3_out);
  and and_3 (and_3_out, not_4_out, not_5_out, Q1, E0);
  and and_4 (and_4_out, Q1, E1);
  and and_5 (and_5_out, not_6_out, Q2, not_7_out);
  and and_6 (and_6_out, Q2, E1);
  and and_7 (and_7_out, Q2, Q1, not_8_out);
  and and_8 (and_8_out, Q3, not_9_out, not_10_out);
  and and_9 (and_9_out, Q3, E1);
  and and_10 (and_10_out, Q3, Q2, E0);
  and and_11 (and_11_out, Q4, not_11_out, not_12_out);
  and and_12 (and_12_out, Q4, not_13_out, REQ, not_14_out);
  and and_13 (and_13_out, Q4, E0);
  and and_14 (and_14_out, E1, E0, REQ, RW);
  and and_15 (and_15_out, not_15_out, Q1, not_16_out, REQ, RW);
  and and_16 (and_16_out, not_17_out, Q1, E0);
  and and_17 (and_17_out, not_18_out, not_19_out, Q1, E1);
  and and_18 (and_18_out, not_20_out, Q2, not_21_out);
  and and_19 (and_19_out, Q2, E0);
  and and_20 (and_20_out, Q3, not_22_out, not_23_out, not_24_out);
  and and_21 (and_21_out, Q3, E1, E0);
  and and_22 (and_22_out, Q3, Q1, not_25_out, not_26_out);
  and and_23 (and_23_out, Q4, not_27_out, not_28_out);
  and and_24 (and_24_out, Q4, E0);
  and and_25 (and_25_out, Q4, Q2);
  and and_26 (and_26_out, Q4, Q3);
  Button button_1 (.out(button_1_out));
  or or_1 (S1, and_1_out, and_2_out, and_3_out, and_4_out, and_5_out, and_6_out, and_7_out, and_8_out, and_9_out, and_10_out, and_11_out, and_12_out, and_13_out);
  or or_2 (S0, and_14_out, and_15_out, and_16_out, and_17_out, and_18_out, and_19_out, and_20_out, and_21_out, and_22_out, and_23_out, and_24_out, and_25_out, and_26_out);
  // Probe on E1
  // Probe on E0
  D_Flip_Flop d_ff_1 (.clk(button_1_out), .D(S1), .Q(E1));  // open: Qn, preset, en, reset
  D_Flip_Flop d_ff_2 (.clk(button_1_out), .D(S0), .Q(E0));  // open: Qn, preset, en, reset
  // Probe on CL
  not not_29 (not_29_out, Q2);
  not not_30 (not_30_out, Q1);
  not not_31 (not_31_out, Q4);
  not not_32 (not_32_out, Q2);
  not not_33 (not_33_out, Q1);
  not not_34 (not_34_out, Q1);
  not not_35 (not_35_out, Q3);
  not not_36 (not_36_out, Q2);
  and and_27 (and_27_out, not_29_out, not_30_out);
  and and_28 (and_28_out, not_31_out, not_32_out, REQ);
  and and_29 (and_29_out, not_33_out, E0);
  and and_30 (and_30_out, not_34_out, E1);
  and and_31 (and_31_out, E1, E0);
  and and_32 (and_32_out, not_35_out, Q2);
  and and_33 (and_33_out, Q3, not_36_out);
  and and_34 (and_34_out, Q3, Q1);
  and and_35 (and_35_out, Q4, E0);
  and and_36 (and_36_out, Q4, E1);
  and and_37 (and_37_out, Q4, Q2);
  not not_37 (not_37_out, Q7S);
  not not_38 (not_38_out, Q6S);
  not not_39 (not_39_out, Q5S);
  not not_40 (not_40_out, Q4S);
  not not_41 (not_41_out, Q3S);
  not not_42 (not_42_out, Q2S);
  not not_43 (not_43_out, Q1S);
  not not_44 (not_44_out, Q9S);
  not not_45 (not_45_out, Q8S);
  not not_46 (not_46_out, Q3S);
  not not_47 (not_47_out, Q2S);
  not not_48 (not_48_out, Q1S);
  not not_49 (not_49_out, Q9S);
  not not_50 (not_50_out, Q8S);
  not not_51 (not_51_out, Q5S);
  not not_52 (not_52_out, Q4S);
  not not_53 (not_53_out, Q1S);
  not not_54 (not_54_out, Q8S);
  not not_55 (not_55_out, Q6S);
  not not_56 (not_56_out, Q4S);
  not not_57 (not_57_out, Q2S);
  or or_3 (CL, and_27_out, and_28_out, and_29_out, and_30_out, and_31_out, and_32_out, and_33_out, and_34_out, and_35_out, and_36_out, and_37_out);
  and and_38 (Q4, not_37_out, not_38_out, not_39_out, not_40_out, not_41_out, not_42_out, not_43_out);
  and and_39 (Q3, not_44_out, not_45_out, not_46_out, not_47_out, not_48_out);
  and and_40 (Q2, not_49_out, not_50_out, not_51_out, not_52_out, not_53_out);
  and and_41 (Q1, not_54_out, not_55_out, not_56_out, not_57_out);
  not not_58 (not_58_out, E0);
  not not_59 (not_59_out, Q1);
  not not_60 (not_60_out, E0);
  not not_61 (not_61_out, Q4);
  not not_62 (not_62_out, E0);
  not not_63 (not_63_out, Q3);
  not not_64 (not_64_out, Q2);
  not not_65 (not_65_out, Q1);
  not not_66 (not_66_out, E0);
  not not_67 (not_67_out, Q4);
  not not_68 (not_68_out, Q3);
  not not_69 (not_69_out, Q4);
  not not_70 (not_70_out, Q2);
  not not_71 (not_71_out, Q3);
  not not_72 (not_72_out, Q2);
  not not_73 (not_73_out, E1);
  not not_74 (not_74_out, E0);
  not not_75 (not_75_out, Q1);
  not not_76 (not_76_out, E1);
  not not_77 (not_77_out, Q3);
  not not_78 (not_78_out, Q2);
  not not_79 (not_79_out, Q4);
  not not_80 (not_80_out, Q2);
  not not_81 (not_81_out, E0);
  not not_82 (not_82_out, Q4);
  not not_83 (not_83_out, E1);
  or or_4 (DOUT, not_58_out, Q3);
  or or_5 (DA, not_59_out, not_60_out, Q3);
  not not_84 (not_84_out, E1);
  and and_42 (and_42_out, not_61_out, Q3, Q2, Q1, not_62_out);
  and and_43 (and_43_out, Q4, not_63_out, not_64_out, not_65_out, not_66_out);
  and and_44 (and_44_out, not_67_out, not_68_out);
  and and_45 (and_45_out, not_69_out, not_70_out);
  and and_46 (and_46_out, not_71_out, not_72_out, not_73_out, not_74_out);
  and and_47 (and_47_out, not_75_out, not_76_out);
  and and_48 (and_48_out, not_77_out, Q1, E1);
  and and_49 (and_49_out, not_78_out, Q1, E1);
  and and_50 (and_50_out, not_79_out, Q3, Q2, Q1, E0);
  and and_51 (and_51_out, Q4, Q1, E1);
  and and_52 (and_52_out, Q3, not_80_out, not_81_out);
  and and_53 (and_53_out, not_82_out, Q3, Q2, Q1, not_83_out, E0);
  or or_6 (WE, not_84_out, and_42_out, and_43_out);
  or or_7 (WC, and_44_out, and_45_out, and_46_out, and_47_out);
  or or_8 (C0, and_48_out, and_49_out, and_50_out, and_51_out);
  or or_9 (C1, and_52_out, and_53_out);
endmodule
