// Logisim project bloco_1.circ as structural Verilog: 1 circuit, main circuit main
module main (
  input  Q1,
  input  Q2,
  input  Q3,
  input  Q4,
  input  REQ,
  input  RW,
  output LD,
  output ES
);

  wire and_1_out, and_2_out, and_3_out, and_4_out, and_5_out, and_6_out, and_7_out, and_8_out, and_9_out,
       and_10_out, and_11_out, not_1_out, not_2_out, not_3_out, not_4_out, not_5_out, not_6_out, not_7_out,
       not_8_out, not_9_out, not_10_out, not_11_out, not_12_out, not_13_out, not_14_out, not_15_out,
       not_16_out, not_17_out, not_18_out, not_19_out, not_20_out, not_21_out;

  not not_1 (not_1_out, Q1);
  not not_2 (not_2_out, Q2);
  not not_3 (not_3_out, Q1);
  not not_4 (not_4_out, Q3);
  not not_5 (not_5_out, RW);
  not not_6 (not_6_out, Q1);
  not not_7 (not_7_out, Q2);
  not not_8 (not_8_out, Q3);
  not not_9 (not_9_out, RW);
  not not_10 (not_10_out, Q2);
  not not_11 (not_11_out, Q4);
  not not_12 (not_12_out, Q1);
  not not_13 (not_13_out, Q2);
  not not_14 (not_14_out, Q3);
  not not_15 (not_15_out, Q4);
  not not_16 (not_16_out, Q3);
  not not_17 (not_17_out, Q4);
  not not_18 (not_18_out, Q2);
  not not_19 (not_19_out, Q3);
  not not_20 (not_20_out, RW);
  not not_21 (not_21_out, Q2);
  and and_1 (and_1_out, not_1_out, not_2_out, Q4);
  and and_2 (and_2_out, not_3_out, not_4_out, Q4, REQ, not_5_out);
  and and_3 (and_3_out, not_6_out, Q3, Q4, REQ, RW);
  and and_4 (and_4_out, Q1, not_7_out, not_8_out, not_9_out);
  and and_5 (and_5_out, Q1, not_10_out, Q3, not_11_out);
  and and_6 (and_6_out, Q1, Q2, Q3, Q4);
  and and_7 (and_7_out, not_12_out, not_13_out, not_14_out, not_15_out, REQ);
  and and_8 (and_8_out, Q2, not_16_out, Q4);
  and and_9 (and_9_out, Q2, Q3, not_17_out);
  and and_10 (and_10_out, Q1, not_18_out, not_19_out, not_20_out);
  and and_11 (and_11_out, Q1, not_21_out, Q4);
  or or_1 (LD, and_1_out, and_2_out, and_3_out, and_4_out, and_5_out, and_6_out);
  or or_2 (ES, and_7_out, and_8_out, and_9_out, and_10_out, and_11_out);
endmodule
