// Logisim project bloco_2.circ as structural Verilog: 1 circuit, main circuit main
module main (
  input  Q1,
  input  Q2,
  input  Q3,
  input  Q4,
  output P1,
  output P2,
  output P3,
  output P4
);

  wire and_1_out, and_3_out, and_4_out, and_5_out, not_1_out, not_2_out, not_3_out, not_4_out, not_5_out,
       not_6_out, not_7_out, not_8_out;

  not not_1 (not_1_out, Q3);
  and and_1 (and_1_out, Q1, Q2);
  not not_2 (not_2_out, Q1);
  and and_2 (P2, not_2_out, not_3_out);
  not not_3 (not_3_out, Q3);
  not not_4 (not_4_out, Q1);
  and and_3 (and_3_out, not_4_out, not_5_out);
  not not_5 (not_5_out, Q3);
  not not_6 (not_6_out, Q1);
  and and_4 (and_4_out, not_6_out, not_7_out);
  not not_7 (not_7_out, Q3);
  not not_8 (not_8_out, Q1);
  and and_5 (and_5_out, not_8_out, Q2);
  or or_1 (P1, not_1_out, and_1_out);
  or or_2 (P3, and_3_out, Q2);
  or or_3 (P4, and_4_out, and_5_out);
endmodule
