// Logisim project bloco_3.circ as structural Verilog: 1 circuit, main circuit main
module main (
  input  Q1,
  input  Q2,
  input  Q3,
  input  Q4,
  output DOUT,
  output DA,
  output WE,
  output WC,
  output C0,
  output C1
);

  wire and_1_out, and_2_out, and_3_out, and_4_out, and_5_out, and_6_out, not_1_out, not_2_out, not_3_out,
       not_4_out, not_5_out, not_6_out, not_7_out, not_8_out, not_9_out, not_10_out, not_11_out, not_12_out,
       not_13_out;

  not not_1 (not_1_out, Q3);
  or or_1 (DOUT, not_1_out, Q2, Q1);
  not not_2 (not_2_out, Q3);
  not not_3 (not_3_out, Q4);
  not not_4 (not_4_out, Q1);
  and and_1 (and_1_out, not_4_out, not_5_out);
  not not_5 (not_5_out, Q2);
  not not_6 (not_6_out, Q2);
  and and_2 (and_2_out, not_6_out, Q3, Q4);
  and and_3 (and_3_out, Q2, not_7_out);
  not not_7 (not_7_out, Q3);
  not not_8 (not_8_out, Q1);
  not not_9 (not_9_out, Q2);
  and and_4 (and_4_out, not_9_out, not_10_out);
  not not_10 (not_10_out, Q3);
  and and_5 (and_5_out, Q2, Q3, Q4);
  and and_6 (and_6_out, Q1, not_11_out, Q4);
  not not_11 (not_11_out, Q3);
  and and_7 (C1, Q1, not_12_out, not_13_out);
  not not_12 (not_12_out, Q2);
  not not_13 (not_13_out, Q3);
  or or_2 (DA, not_2_out, not_3_out, Q2, Q1);
  or or_3 (WE, and_1_out, and_2_out, and_3_out);
  or or_4 (WC, not_8_out, and_4_out);
  or or_5 (C0, and_5_out, and_6_out);
endmodule
